// Logisim project CPU.circ as structural Verilog: 5 circuits, main circuit main
module main (
  input  pcoe,
  input  pcce,
  input  ramwe,
  input  [15:0] Testing_Data,
  input  ramoe,
  input  OE_TESTING,
  input  mbrwe,
  input  in_8,
  input  mbribe,
  input  mbroe,
  input  [7:0] in_11,
  input  irwe,
  input  reset_mar,
  input  iroe,
  input  marwe,
  input  maroe,
  input  aluoe,
  input  regawe,
  input  regbwe,
  input  oroe,
  input  reset_ir,
  input  orwe,
  input  reset_ra,
  input  [2:0] ru_selector,
  input  reset_mbr,
  input  [3:0] au_selector,
  input  reset_rb,
  input  reset,
  output [3:0] pc_disp,
  output op0,
  output op1,
  output op2,
  output op3,
  output op4,
  output [7:0] mar_out,
  output [7:0] counter_content,
  output op5,
  output op6,
  output op7,
  output [15:0] ir_out,
  output sc0,
  output sc1,
  output sc2,
  output [15:0] rega_out,
  output out_45,
  output [15:0] mbr_out,
  output [15:0] alu_out,
  output [2:0] sc_content,
  output [3:0] sc_disp,
  output [15:0] regb_out,
  output [3:0] rega_disp,
  output [3:0] rega_disp_1,
  output [3:0] rega_disp_2,
  output [3:0] rega_disp_3,
  output [3:0] rega_disp_4,
  output [3:0] or_disp,
  output [3:0] or_disp_1,
  output [3:0] or_disp_2,
  output [3:0] or_disp_3,
  output [3:0] or_disp_4,
  output [3:0] regb_disp,
  output [3:0] regb_disp_1,
  output [3:0] regb_disp_2,
  output [3:0] regb_disp_3,
  output [3:0] regb_disp_4,
  output [3:0] alu_disp,
  output [3:0] alu_disp_1,
  output [3:0] alu_disp_2,
  output [3:0] alu_disp_3,
  output [3:0] alu_disp_4
);

  wire CLK_out;
  wire [7:0] controlled_buffer_1_out, controlled_buffer_7_out;
  wire [15:0] bit_extender_1_out, bit_extender_2_out, controlled_buffer_2_out, controlled_buffer_3_out,
       OUTPUT_REG_q, ram_1_dout;
  wire [19:4] decimal_decoder_64331049_1_out_2, decimal_decoder_64331049_6_out_2;

  Clock CLK (.out(CLK_out));
  assign bit_extender_1_out = {{8{counter_content[7]}}, counter_content};  // Bit_Extender bit_extender_1
  Counter #(.max('h3)) Program_Counter_25da0db7 (
    .count(pcce), .clk(CLK_out), .D(controlled_buffer_1_out), .Q(counter_content));  // open: clr, load, up, carry
  Decimal_Decoder_64331049 decimal_decoder_64331049_1 (
    .Din(bit_extender_1_out), .out_2({decimal_decoder_64331049_1_out_2, pc_disp}));
  Decimal_Decoder_64331049 decimal_decoder_64331049_2 (
    .Din(rega_out), .out_2({rega_disp, rega_disp_1, rega_disp_2, rega_disp_3, rega_disp_4}));
  Decimal_Decoder_64331049 decimal_decoder_64331049_3 (
    .Din(regb_out), .out_2({regb_disp, regb_disp_1, regb_disp_2, regb_disp_3, regb_disp_4}));
  assign controlled_buffer_1_out = pcoe ? counter_content : 8'bz;  // Controlled_Buffer controlled_buffer_1
  Register #(.width(16)) IR (.D(controlled_buffer_3_out), .en(irwe), .clk(CLK_out), .Q(ir_out), .clr(reset_ir));
  Register #(.width(16)) register_a (
    .D(controlled_buffer_3_out), .en(regawe), .clk(CLK_out), .Q(rega_out), .clr(reset_ra));
  Register #(.width(16)) register_b (
    .D(controlled_buffer_3_out), .en(regbwe), .clk(CLK_out), .Q(regb_out), .clr(reset_rb));
  assign controlled_buffer_2_out = iroe ? ir_out : 16'bz;  // Controlled_Buffer controlled_buffer_2
  project_alu project_alu_1 (
    .A(rega_out), .B(regb_out), .RUSel(ru_selector), .AUSel(au_selector), .RUResult(out_45), .Dout(alu_out));  // open: AUResult
  Decimal_Decoder_64331049 decimal_decoder_64331049_4 (
    .Din(alu_out), .out_2({alu_disp, alu_disp_1, alu_disp_2, alu_disp_3, alu_disp_4}));
  BitSelector #(.group(8), .width(16)) bitselector_1 (
    .in(controlled_buffer_2_out), .out(controlled_buffer_1_out), .sel(1'b0));
  assign controlled_buffer_3_out = aluoe ? alu_out : 16'bz;  // Controlled_Buffer controlled_buffer_3
  LED led_1 (.in(controlled_buffer_3_out[15]));
  LED led_2 (.in(controlled_buffer_3_out[14]));
  LED led_3 (.in(controlled_buffer_3_out[13]));
  LED led_4 (.in(controlled_buffer_3_out[12]));
  LED led_5 (.in(controlled_buffer_3_out[11]));
  LED led_6 (.in(controlled_buffer_3_out[10]));
  LED led_7 (.in(controlled_buffer_3_out[9]));
  LED led_8 (.in(controlled_buffer_3_out[8]));
  assign controlled_buffer_3_out = OE_TESTING ? Testing_Data : 16'bz;  // Controlled_Buffer controlled_buffer_4
  LED led_9 (.in(controlled_buffer_3_out[7]));
  LED led_10 (.in(controlled_buffer_3_out[6]));
  LED led_11 (.in(controlled_buffer_3_out[5]));
  LED led_12 (.in(controlled_buffer_3_out[4]));
  LED led_13 (.in(controlled_buffer_3_out[3]));
  LED led_14 (.in(controlled_buffer_3_out[2]));
  LED led_15 (.in(controlled_buffer_3_out[1]));
  LED led_16 (.in(controlled_buffer_3_out[0]));
  Register register_1 (.D(controlled_buffer_1_out), .en(marwe), .clk(CLK_out), .Q(mar_out), .clr(reset_mar));
  Decimal_Decoder_64331049 decimal_decoder_64331049_5 (
    .Din(OUTPUT_REG_q), .out_2({or_disp, or_disp_1, or_disp_2, or_disp_3, or_disp_4}));
  assign controlled_buffer_3_out = mbribe ? mbr_out : 16'bz;  // Controlled_Buffer controlled_buffer_5
  assign controlled_buffer_3_out = oroe ? OUTPUT_REG_q : 16'bz;  // Controlled_Buffer controlled_buffer_6
  assign controlled_buffer_7_out = maroe ? mar_out : 8'bz;  // Controlled_Buffer controlled_buffer_7
  Register #(.width(16)) MBR (.D(controlled_buffer_3_out), .en(mbrwe), .clk(CLK_out), .Q(mbr_out), .clr(reset_mbr));
  Register #(.width(16)) OUTPUT_REG (
    .D(controlled_buffer_3_out), .en(orwe), .clk(CLK_out), .Q(OUTPUT_REG_q), .clr(reset));
  assign controlled_buffer_3_out = mbroe ? mbr_out : 16'bz;  // Controlled_Buffer controlled_buffer_8
  assign controlled_buffer_7_out = in_8 ? in_11 : 8'bz;  // Controlled_Buffer controlled_buffer_9
  LED led_17 (.in(controlled_buffer_3_out[15]));
  LED led_18 (.in(controlled_buffer_3_out[14]));
  LED led_19 (.in(controlled_buffer_3_out[13]));
  LED led_20 (.in(controlled_buffer_3_out[12]));
  LED led_21 (.in(controlled_buffer_3_out[11]));
  LED led_22 (.in(controlled_buffer_3_out[10]));
  LED led_23 (.in(controlled_buffer_3_out[9]));
  LED led_24 (.in(controlled_buffer_3_out[8]));
  LED led_25 (.in(controlled_buffer_3_out[7]));
  LED led_26 (.in(controlled_buffer_3_out[6]));
  LED led_27 (.in(controlled_buffer_3_out[5]));
  LED led_28 (.in(controlled_buffer_3_out[4]));
  LED led_29 (.in(controlled_buffer_3_out[3]));
  LED led_30 (.in(controlled_buffer_3_out[2]));
  LED led_31 (.in(controlled_buffer_3_out[1]));
  LED led_32 (.in(controlled_buffer_3_out[0]));
  assign controlled_buffer_3_out = ramoe ? ram_1_dout : 16'bz;  // Controlled_Buffer controlled_buffer_10
  Counter #(.max('h5), .width(3)) Step_counter (
    .clk(CLK_out), .Q({sc2, sc1, sc0}));  // open: clr, load, up, count, D, carry
  RAM #(.dataWidth(16), .enables("line"), .\type ("nonvolatile")) ram_1 (
    .addr(controlled_buffer_7_out), .we(ramwe), .clk(CLK_out), .din(controlled_buffer_3_out),
    .dout(ram_1_dout));
  BitSelector #(.group(8), .width(16)) bitselector_2 (
    .in(ir_out), .out({op7, op6, op5, op4, op3, op2, op1, op0}), .sel(1'b1));
  assign bit_extender_2_out = {{13{1'b0}}, {sc2, sc1, sc0}};  // Bit_Extender bit_extender_2
  Decimal_Decoder_64331049 decimal_decoder_64331049_6 (
    .Din(bit_extender_2_out), .out_2({decimal_decoder_64331049_6_out_2, sc_disp}));

  assign sc_content = {sc2, sc1, sc0};

  // Notes on the sheet:
  //   Internal Address Bus
  //   Internal Data Bus
  //   External Address Bus
  //   External Data Bus
  //   pc_oe
  //   pc_count_enable
  //   ram we
  //   ram oe
  //   mbr we
  //   mbr internal bus enable
  //   mbr oe
  //   ir we
  //   ir oe
  //   mar we
  //   mar oe
  //   ALU oe
  //   Reg_A we
  //   Reg_B we
  //   Output register Oe
  //   Output register we
endmodule

module Decimal_Decoder_64331049 (
  input  [15:0] Din,
  output [19:0] out_2
);

  ROM #(.addrWidth(16), .dataWidth(20)) rom_1 (.addr(Din), .data(out_2));

  // Notes on the sheet:
  //   contents of rom_1 (hex, n*v repeats v):
  //   0 1 2 3 4 5 6 7 8 9 10 11 12 13 14 15 16 17 18 19 20 21 22 23 24 25 26 27 28 29 30 31 32 33 34 35 36
  //   37 38 39 40 41 42 43 44 45 46 47 48 49 50 51 52 53 54 55 56 57 58 59 60 61 62 63 64 65 66 67 68 69
  //   70 71 72 73 74 75 76 77 78 79 80 81 82 83 84 85 86 87 88 89 90 91 92 93 94 95 96 97 98 99 100 101
  //   102 103 104 105 106 107 108 109 110 111 112 113 114 115 116 117 118 119 120 121 122 123 124 125 126
  //   127 128 129 130 131 132 133 134 135 136 137 138 139 140 141 142 143 144 145 146 147 148 149 150 151
  //   152 153 154 155 156 157 158 159 160 161 162 163 164 165 166 167 168 169 170 171 172 173 174 175 176
  //   177 178 179 180 181 182 183 184 185 186 187 188 189 190 191 192 193 194 195 196 197 198 199 200 201
  //   202 203 204 205 206 207 208 209 210 211 212 213 214 215 216 217 218 219 220 221 222 223 224 225 226
  //   227 228 229 230 231 232 233 234 235 236 237 238 239 240 241 242 243 244 245 246 247 248 249 250 251
  //   252 253 254 255 256 257 258 259 260 261 262 263 264 265 266 267 268 269 270 271 272 273 274 275 276
  //   277 278 279 280 281 282 283 284 285 286 287 288 289 290 291 292 293 294 295 296 297 298 299 300 301
  //   302 303 304 305 306 307 308 309 310 311 312 313 314 315 316 317 318 319 320 321 322 323 324 325 326
  //   327 328 329 330 331 332 333 334 335 336 337 338 339 340 341 342 343 344 345 346 347 348 349 350 351
  //   352 353 354 355 356 357 358 359 360 361 362 363 364 365 366 367 368 369 370 371 372 373 374 375 376
  //   377 378 379 380 381 382 383 384 385 386 387 388 389 390 391 392 393 394 395 396 397 398 399 400 401
  //   402 403 404 405 406 407 408 409 410 411 412 413 414 415 416 417 418 419 420 421 422 423 424 425 426
  //   427 428 429 430 431 432 433 434 435 436 437 438 439 440 441 442 443 444 445 446 447 448 449 450 451
  //   452 453 454 455 456 457 458 459 460 461 462 463 464 465 466 467 468 469 470 471 472 473 474 475 476
  //   477 478 479 480 481 482 483 484 485 486 487 488 489 490 491 492 493 494 495 496 497 498 499 500 501
  //   502 503 504 505 506 507 508 509 510 511 512 513 514 515 516 517 518 519 520 521 522 523 524 525 526
  //   527 528 529 530 531 532 533 534 535 536 537 538 539 540 541 542 543 544 545 546 547 548 549 550 551
  //   552 553 554 555 556 557 558 559 560 561 562 563 564 565 566 567 568 569 570 571 572 573 574 575 576
  //   577 578 579 580 581 582 583 584 585 586 587 588 589 590 591 592 593 594 595 596 597 598 599 600 601
  //   602 603 604 605 606 607 608 609 610 611 612 613 614 615 616 617 618 619 620 621 622 623 624 625 626
  //   627 628 629 630 631 632 633 634 635 636 637 638 639 640 641 642 643 644 645 646 647 648 649 650 651
  //   652 653 654 655 656 657 658 659 660 661 662 663 664 665 666 667 668 669 670 671 672 673 674 675 676
  //   677 678 679 680 681 682 683 684 685 686 687 688 689 690 691 692 693 694 695 696 697 698 699 700 701
  //   702 703 704 705 706 707 708 709 710 711 712 713 714 715 716 717 718 719 720 721 722 723 724 725 726
  //   727 728 729 730 731 732 733 734 735 736 737 738 739 740 741 742 743 744 745 746 747 748 749 750 751
  //   752 753 754 755 756 757 758 759 760 761 762 763 764 765 766 767 768 769 770 771 772 773 774 775 776
  //   777 778 779 780 781 782 783 784 785 786 787 788 789 790 791 792 793 794 795 796 797 798 799 800 801
  //   802 803 804 805 806 807 808 809 810 811 812 813 814 815 816 817 818 819 820 821 822 823 824 825 826
  //   827 828 829 830 831 832 833 834 835 836 837 838 839 840 841 842 843 844 845 846 847 848 849 850 851
  //   852 853 854 855 856 857 858 859 860 861 862 863 864 865 866 867 868 869 870 871 872 873 874 875 876
  //   877 878 879 880 881 882 883 884 885 886 887 888 889 890 891 892 893 894 895 896 897 898 899 900 901
  //   902 903 904 905 906 907 908 909 910 911 912 913 914 915 916 917 918 919 920 921 922 923 924 925 926
  //   927 928 929 930 931 932 933 934 935 936 937 938 939 940 941 942 943 944 945 946 947 948 949 950 951
  //   952 953 954 955 956 957 958 959 960 961 962 963 964 965 966 967 968 969 970 971 972 973 974 975 976
  //   977 978 979 980 981 982 983 984 985 986 987 988 989 990 991 992 993 994 995 996 997 998 999 1000
  //   1001 1002 1003 1004 1005 1006 1007 1008 1009 1010 1011 1012 1013 1014 1015 1016 1017 1018 1019 1020
  //   1021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
endmodule

module CU (
  input  OPC3,
  input  OPC2,
  input  OPC1,
  input  OPC0,
  input  SC2,
  input  SC1,
  input  SC0,
  output C0,
  output C1,
  output C2,
  output C3,
  output C4,
  output C5,
  output C6,
  output C7,
  output C8,
  output C9,
  output C10,
  output C11,
  output C12,
  output C13,
  output C14,
  output C15
);

  wire and_4_out, and_5_out, and_6_out, and_7_out, and_8_out, and_9_out, and_10_out, and_13_out, and_14_out,
       and_15_out, and_16_out, and_17_out, and_18_out, and_19_out, and_20_out, not_1_out, not_2_out,
       not_3_out, not_4_out, not_5_out;

  not not_1 (not_1_out, OPC1);
  not not_2 (not_2_out, OPC0);
  not not_3 (not_3_out, SC2);
  not not_4 (not_4_out, SC1);
  not not_5 (not_5_out, SC0);
  and and_1 (C0, not_3_out, not_4_out, not_5_out);
  and and_2 (C1, not_3_out, not_4_out, SC0);
  and and_3 (C2, OPC1, OPC0, SC2, not_4_out, not_5_out);
  and and_4 (and_4_out, not_3_out, not_4_out, SC0);
  and and_5 (and_5_out, not_1_out, SC2, not_4_out, not_5_out);
  and and_6 (and_6_out, not_3_out, not_4_out, SC0);
  and and_7 (and_7_out, not_1_out, SC2, not_4_out, not_5_out);
  and and_8 (and_8_out, OPC1, OPC0, not_3_out, SC0);
  and and_9 (and_9_out, not_3_out, SC1, not_5_out);
  and and_10 (and_10_out, not_1_out, SC2, not_4_out, SC0);
  and and_11 (C6, OPC1, OPC0, SC2, not_4_out, not_5_out);
  and and_12 (C7, not_3_out, SC1, not_5_out);
  and and_13 (and_13_out, not_1_out, not_3_out, SC1, SC0);
  and and_14 (and_14_out, OPC0, not_3_out, SC1, SC0);
  and and_15 (and_15_out, not_3_out, not_4_out, not_5_out);
  and and_16 (and_16_out, not_1_out, not_3_out, SC1, SC0);
  and and_17 (and_17_out, OPC0, not_3_out, SC1, SC0);
  and and_18 (and_18_out, not_3_out, not_4_out, SC0);
  and and_19 (and_19_out, not_1_out, SC2, not_4_out, not_5_out);
  and and_20 (and_20_out, OPC0, SC2, not_4_out, not_5_out);
  and and_21 (C11, OPC1, not_2_out, not_3_out, SC1, SC0);
  and and_22 (C12, not_1_out, not_2_out, SC2, not_4_out, SC0);
  and and_23 (C13, not_1_out, OPC0, SC2, not_4_out, SC0);
  and and_24 (C14, OPC1, OPC0, not_3_out, SC1, SC0);
  and and_25 (C15, OPC1, not_2_out, not_3_out, SC1, SC0);
  or or_1 (C3, and_4_out, and_5_out);
  or or_2 (C4, and_6_out, and_7_out, and_8_out);
  or or_3 (C5, and_9_out, and_10_out);
  or or_4 (C8, and_13_out, and_14_out);
  or or_5 (C9, and_15_out, and_16_out, and_17_out);
  or or_6 (C10, and_18_out, and_19_out, and_20_out);
endmodule

module CU2 (
  input  OPC7,
  input  OPC6,
  input  OPC5,
  input  OPC4,
  input  OPC3,
  input  OPC2,
  input  OPC1,
  input  OPC0,
  input  SC2,
  input  SC1,
  input  SC0,
  output C0,
  output C1,
  output C2,
  output C3,
  output C4,
  output C5,
  output C6,
  output C7,
  output C8,
  output C9,
  output C10,
  output C11,
  output C12,
  output C13,
  output C14,
  output C15
);

  wire and_4_out, and_5_out, and_6_out, and_7_out, and_8_out, and_9_out, and_10_out, and_13_out, and_14_out,
       and_15_out, and_16_out, and_17_out, and_18_out, and_19_out, not_1_out, not_2_out, not_3_out,
       not_4_out, not_5_out;

  not not_1 (not_1_out, OPC1);
  not not_2 (not_2_out, OPC0);
  not not_3 (not_3_out, SC2);
  not not_4 (not_4_out, SC1);
  not not_5 (not_5_out, SC0);
  and and_1 (C0, not_3_out, not_4_out, not_5_out);
  and and_2 (C1, not_3_out, not_4_out, SC0);
  and and_3 (C2, OPC1, SC2);
  and and_4 (and_4_out, not_3_out, not_4_out, SC0);
  and and_5 (and_5_out, not_1_out, SC2, not_5_out);
  and and_6 (and_6_out, not_3_out, not_4_out, SC0);
  and and_7 (and_7_out, OPC1, OPC0, SC0);
  and and_8 (and_8_out, not_1_out, SC2, not_5_out);
  and and_9 (and_9_out, SC1, not_5_out);
  and and_10 (and_10_out, SC2, SC0);
  and and_11 (C6, OPC1, SC2);
  and and_12 (C7, SC1, not_5_out);
  and and_13 (and_13_out, not_1_out, SC1, SC0);
  and and_14 (and_14_out, OPC0, SC1, SC0);
  and and_15 (and_15_out, not_3_out, not_4_out, not_5_out);
  and and_16 (and_16_out, not_1_out, SC1, SC0);
  and and_17 (and_17_out, OPC0, SC1, SC0);
  and and_18 (and_18_out, not_3_out, not_4_out, SC0);
  and and_19 (and_19_out, SC2, not_5_out);
  and and_20 (C11, OPC1, not_2_out, SC1, SC0);
  and and_21 (C12, not_2_out, SC2, SC0);
  and and_22 (C13, OPC0, SC2, SC0);
  and and_23 (C14, OPC1, OPC0, SC1, SC0);
  and and_24 (C15, OPC1, not_2_out, SC1, SC0);
  or or_1 (C3, and_4_out, and_5_out);
  or or_2 (C4, and_6_out, and_7_out, and_8_out);
  or or_3 (C5, and_9_out, and_10_out);
  or or_4 (C8, and_13_out, and_14_out);
  or or_5 (C9, and_15_out, and_16_out, and_17_out);
  or or_6 (C10, and_18_out, and_19_out);
endmodule

module CPU (
  input  [3:0] au_sel,
  input  [2:0] ru_sel,
  output [15:0] registerA_out,
  output [7:0] pc_content,
  output [15:0] registerB_out,
  output [2:0] sc_content,
  output [15:0] MBR_out,
  output [15:0] ALU_out,
  output [15:0] IR_out,
  output [7:0] MAR_out
);

  wire main_1_p1, main_1_p2, main_1_p3, main_1_p4, main_1_p5, main_1_p6, main_1_p7, main_1_p8, main_1_p9,
       main_1_p10, main_1_p11, main_1_p12, main_1_p13, main_1_p14, main_1_p15, main_1_p16, main_1_p27,
       main_1_p28, main_1_p29, main_1_p30, main_1_p31, main_1_p32, main_1_p33, main_1_p34, main_1_p35,
       main_1_p36, main_1_p37;

  // main main_1: pin names not known; wires that end beside it: main_1_p1, main_1_p2, main_1_p3, main_1_p4, main_1_p5, main_1_p6, main_1_p7, main_1_p8, main_1_p9, main_1_p10, main_1_p11, main_1_p12, main_1_p13, main_1_p14, main_1_p15, main_1_p16, pc_content, sc_content, au_sel, ru_sel, registerA_out, registerB_out, MBR_out, ALU_out, IR_out, MAR_out, main_1_p27, main_1_p28, main_1_p29, main_1_p30, main_1_p31, main_1_p32, main_1_p33, main_1_p34, main_1_p35, main_1_p36, main_1_p37
  // CU2 cu2_1: pin names not known; wires that end beside it: main_1_p34, main_1_p33, main_1_p32, main_1_p31, main_1_p30, main_1_p29, main_1_p28, main_1_p27, main_1_p36, main_1_p37, main_1_p35, main_1_p1, main_1_p2, main_1_p3, main_1_p4, main_1_p5, main_1_p6, main_1_p7, main_1_p8, main_1_p9, main_1_p10, main_1_p11, main_1_p12, main_1_p13, main_1_p14, main_1_p15, main_1_p16

  // Notes on the sheet:
  //   pc_oe
  //   pc_count_enable
  //   ram we
  //   ram oe
  //   mbr we
  //   mbr_ibe
  //   mbr oe
  //   ir we
  //   ir oe
  //   mar we
  //   mar oe
  //   ALU oe
  //   Reg_A we
  //   Reg_B we
  //   Output register Oe
  //   Output register we
  //   pc_oe
  //   ram oe
  //   mbr_ibe
  //   mbr oe
  //   ir we
  //   ir oe
  //   mar we
  //   mar oe
  //   ALU oe
  //   pc_count_enable
  //   ram we
  //   mbr we
  //   Reg_A we
  //   Reg_B we
  //   Output register Oe
  //   Output register we
endmodule
